# Fritzing sketch RuLEDta_Schematic (saved by Fritzing 0.9.6b)
breadboards: 1

parts:
  부품2 = Arduino Uno (Rev3)
  NEOPIXEL1 = Neopixel Strip -- Black (30/m)
  Matrix_keypad1 = KEYPAD 4x4
  Part1 = LCD1602-I2C
  S1 = SWITCH-MOMENTARY-2 [package=tactile-pth-12mm]
  DFRobot_DFPlayer_Mini1 = DFRobot DFPlayer Mini [part_number=DFR0299]
  SPKR1 = Loudspeaker
  SPKR2 = Loudspeaker
  R1 = Resistor [tolerance=±5% resistance=1k package="0402 [SMD]"]
  R2 = Resistor [tolerance=±5% resistance=1k package="0402 [SMD]"]
  부품1 = Breadboard Power Supply Board SMD

nets:
  N1: 부품2.A4/SDA, Part1.SDA
  N2: 부품2.A5/SCL, Part1.SCL
  N3: 부품2.D8, Matrix_keypad1.row1
  N4: 부품2.D9_PWM, Matrix_keypad1.row2
  N5: 부품2.D10_PWM/SS, Matrix_keypad1.row3
  N6: 부품2.D11_PWM/MOSI, Matrix_keypad1.row4
  N7: 부품2.D12/MISO, S1.2
  GND: 부품2.GND, NEOPIXEL1.GND, Part1.GND, S1.1, DFRobot_DFPlayer_Mini1.GND-1, DFRobot_DFPlayer_Mini1.GND-2, SPKR1.pin1, SPKR2.pin1, 부품1.GND
  N8: 부품2.D0/RX, R2.Pin_0
  N9: 부품2.D1/TX, R1.Pin_0
  N10: 부품2.D2, NEOPIXEL1.DI
  N11: 부품2.D4, Matrix_keypad1.col1
  N12: 부품2.D5_PWM, Matrix_keypad1.col2
  N13: 부품2.D6_PWM, Matrix_keypad1.col3
  N14: 부품2.D7, Matrix_keypad1.col4
  VCC: NEOPIXEL1.+5V, Part1.VCC, DFRobot_DFPlayer_Mini1.VCC, 부품1.VCC
  N15: DFRobot_DFPlayer_Mini1.RX, R1.Pin_1
  N16: DFRobot_DFPlayer_Mini1.TX, R2.Pin_1
  N17: DFRobot_DFPlayer_Mini1.DAC_R, SPKR1.pin2
  N18: DFRobot_DFPlayer_Mini1.DAC_L, SPKR2.pin2

custom parts:
  Neopixel Strip -- Black (30/m): Neopixel Strip, Black, 30 pixels per meter.
  KEYPAD 4x4: Matrix keypad 16 buttons, 4 rows x 4 columns
  LCD1602-I2C: A standard character display, usually with 2x16 characters. Comes in many colors with LCM1602 IIC attached.
